// Logisim project myCirc.circ as structural Verilog: 4 circuits, main circuit main
module main (
  input  [15:0] B,
  input  [15:0] A
);

  small_ALU small_alu_1 ();  // open: A_s_exponent, B_s_exponent, out_3
  big_ALU big_alu_1 ();  // open: A, B, sign_A, sign_B, output, carry_out, sign_bit_output
  Normalize normalize_1 ();  // open: fraction, exponent, carry, out_4, out_5, Exponent_out_of_range
endmodule

module small_ALU (
  input  [3:0] A_s_exponent,
  input  [3:0] B_s_exponent,
  output [3:0] out_3
);

  wire subtractor_1_bout;
  wire [3:0] negator_1_out, subtractor_1_out;

  Subtractor #(.width(4)) subtractor_1 (
    .a(A_s_exponent), .b(B_s_exponent), .out(subtractor_1_out), .bout(subtractor_1_bout));  // open: bin
  Negator #(.width(4)) negator_1 (.in(subtractor_1_out), .out(negator_1_out));
  Multiplexer #(.width(4), .enable("false")) multiplexer_1 (
    .in0(subtractor_1_out), .in1(negator_1_out), .out(out_3), .sel(subtractor_1_bout));

  // Notes on the sheet:
  //   sign bit
  //   absolute exponent difference
endmodule

module big_ALU (
  input  [11:0] A,
  input  [11:0] B,
  input  sign_A,
  input  sign_B,
  input  sign_bit_output,
  output [11:0] \output ,
  output carry_out
);

  wire adder_1_cout, comparator_1_gt, multiplexer_1_out, subtractor_1_bout, xor_1_out;
  wire [11:0] adder_1_out, multiplexer_2_out, negator_1_out, subtractor_1_out;

  xor xor_1 (xor_1_out, sign_A, sign_B);
  Adder #(.width(12)) adder_1 (.a(A), .b(B), .out(adder_1_out), .cout(adder_1_cout));  // open: cin
  Subtractor #(.width(12)) subtractor_1 (.a(A), .b(B), .out(subtractor_1_out), .bout(subtractor_1_bout));  // open: bin
  Comparator #(.width(12), .mode("unsigned")) comparator_1 (.a(A), .b(B), .gt(comparator_1_gt));  // open: eq, lt
  Negator #(.width(12)) negator_1 (.in(subtractor_1_out), .out(negator_1_out));
  Multiplexer #(.enable("false")) multiplexer_1 (
    .in0(sign_B), .in1(sign_A), .out(multiplexer_1_out), .sel(comparator_1_gt));
  Multiplexer #(.width(12), .enable("false")) multiplexer_2 (
    .in0(subtractor_1_out), .in1(negator_1_out), .out(multiplexer_2_out), .sel(subtractor_1_bout));
  Multiplexer #(.enable("false")) multiplexer_3 (
    .in0(subtractor_1_bout), .in1(adder_1_cout), .out(carry_out), .sel(xor_1_out));
  Multiplexer #(.width(12), .enable("false")) multiplexer_4 (
    .in0(adder_1_out), .in1(multiplexer_2_out), .out(\output ), .sel(xor_1_out));
  Multiplexer #(.enable("false")) multiplexer_5 (
    .in0(sign_B), .in1(multiplexer_1_out), .out(sign_bit_output), .sel(xor_1_out));

  // Notes on the sheet:
  //   A>B?
  //   sum
  //   absolute difference
  //   IF signs same, return B's sign, else return greater val's sign
endmodule

module Normalize (
  input  [11:0] fraction,
  input  [3:0] exponent,
  input  carry,
  output [10:0] out_4,
  output [3:0] out_5,
  output Exponent_out_of_range
);

  wire [3:0] adder_1_out, bit_extender_1_out, bitfinder_1_index, subtractor_1_out;
  wire [11:0] adder_2_out, bit_extender_2_out, shifter_1_out, shifter_2_out;
  wire [11:11] shifter_3_out;

  assign bit_extender_1_out = {{3{1'b0}}, carry};  // Bit_Extender bit_extender_1
  Shifter #(.width(12), .shift("lr")) shifter_1 (.in(fraction), .\dist (bit_extender_1_out), .out(shifter_1_out));
  assign bit_extender_2_out = {{11{1'b0}}, carry};  // Bit_Extender bit_extender_2
  Adder #(.width(4)) adder_1 (.a(exponent), .b(bit_extender_1_out), .out(adder_1_out));  // open: cin, cout
  Shifter #(.width(12)) shifter_2 (.in(bit_extender_2_out), .\dist (4'b1011), .out(shifter_2_out));
  Adder #(.width(12)) adder_2 (.a(shifter_1_out), .b(shifter_2_out), .out(adder_2_out));  // open: cin, cout
  BitFinder #(.width(12), .\type ("high1")) bitfinder_1 (.in(adder_2_out), .index(bitfinder_1_index));  // open: found
  Subtractor #(.width(4)) subtractor_1 (.a(4'b1011), .b(bitfinder_1_index), .out(subtractor_1_out));  // open: bin, bout
  Shifter #(.width(12)) shifter_3 (.in(adder_2_out), .\dist (subtractor_1_out), .out({shifter_3_out[11], out_4}));
  Subtractor #(.width(4)) subtractor_2 (
    .a(adder_1_out), .b(subtractor_1_out), .out(out_5), .bout(Exponent_out_of_range));  // open: bin

  // Notes on the sheet:
  //   the ckt shifts right once if carry = 1, then gives that as output
  //   add 1 to exponent if carry = 1
  //   adding carry to msb
  //   amount by which fraction is left shifted
endmodule
